# Fritzing sketch Proje çizimi (saved by Fritzing 0.9.5d)
breadboards: 1

parts:
  RFID_Okuyucu = RFID-RC522-v2
  Buzzer = Piezo Speaker
  RGB_LED = RGB LED (com. cathode, rgb) [package="5 mm [THT]"]
  R1 = Resistor [tolerance=±5% resistance=220 package=THT]
  Arduino_Nano = Arduino Nano (Rev3.0)
  Ayar_Butonu = Pushbutton [package="[THT]"]
  R2 = Resistor [tolerance=±5% resistance=1k package=THT]

nets:
  N1: RFID_Okuyucu.SDA, Arduino_Nano.D10
  N2: RFID_Okuyucu.SCK, Arduino_Nano.D13/SCK
  N3: RFID_Okuyucu.MOSI, Arduino_Nano.D11/MOSI
  N4: RFID_Okuyucu.MISO, Arduino_Nano.D12/MISO
  GND: RFID_Okuyucu.GND, Buzzer.pin1, R1.Pin_0, Arduino_Nano.GND, R2.Pin_1
  N5: RFID_Okuyucu.RST, Arduino_Nano.D9
  3.3V: RFID_Okuyucu.3.3V, Arduino_Nano.3V3, Ayar_Butonu.Pin_3, Ayar_Butonu.Pin_4
  N6: Buzzer.pin2, Arduino_Nano.D8
  N7: RGB_LED.red_anode, Arduino_Nano.A0
  N8: RGB_LED.common_cathode, R1.Pin_1
  N9: RGB_LED.green_anode, Arduino_Nano.A1
  N10: RGB_LED.blue_anode, Arduino_Nano.A2
  N11: Arduino_Nano.D7, Ayar_Butonu.Pin_1, Ayar_Butonu.Pin_2, R2.Pin_0

custom parts:
  RFID-RC522-v2: A simple China made RFID-RC522 Reader; do check the pin labels, as this is a MFRC522 based clone.
